// Logisim project slt_8bits.circ as structural Verilog: 3 circuits, main circuit SLT8bits
module SLT8bits (
  input  [7:0] A,
  input  [7:0] B,
  output [7:0] S
);

  wire slt_eqin_1_s, slt_eqout_1_eq, slt_eqout_1_s;

  SLT_EqOUT slt_eqout_1 (.A(A[7:4]), .B(B[7:4]), .Eq(slt_eqout_1_eq), .S(slt_eqout_1_s));
  SLT_EqIN slt_eqin_1 (.A(A[3:0]), .B(B[3:0]), .Eq(slt_eqout_1_eq), .S(slt_eqin_1_s));
  or or_1 (S[7], slt_eqout_1_s, slt_eqin_1_s);

  assign S[6:0] = {7{S[7]}};
endmodule

// 1/2
module SLT_EqOUT (
  input  [3:0] A,
  input  [3:0] B,
  output S,
  output Eq
);

  wire and_1_out, and_2_out, and_3_out, and_4_out, and_5_out, and_6_out, and_7_out, xnor_1_out, xnor_2_out,
       xnor_3_out;

  and and_1 (and_1_out, ~A[3], B[3]);  // AND_Gate
  xnor xnor_1 (xnor_1_out, A[3], B[3]);
  and and_2 (and_2_out, ~A[2], B[2]);  // AND_Gate
  xnor xnor_2 (xnor_2_out, A[2], B[2]);
  and and_3 (and_3_out, ~A[1], B[1]);  // AND_Gate
  xnor xnor_3 (xnor_3_out, A[1], B[1]);
  and and_4 (and_4_out, ~A[0], B[0]);  // AND_Gate
  and and_5 (and_5_out, xnor_1_out, and_2_out);
  and and_6 (and_6_out, xnor_1_out, xnor_2_out, and_3_out);
  and and_7 (and_7_out, xnor_1_out, xnor_2_out, xnor_3_out, and_4_out);
  and and_8 (Eq, xnor_1_out, xnor_2_out, xnor_3_out);
  or or_1 (S, and_1_out, and_5_out, and_6_out, and_7_out);
endmodule

// SLT
module SLT_EqIN (
  input  Eq,
  input  [3:0] A,
  input  [3:0] B,
  output S
);

  wire and_1_out, and_2_out, and_3_out, and_4_out, and_5_out, and_6_out, and_7_out, xnor_1_out, xnor_2_out,
       xnor_3_out;

  and and_1 (and_1_out, ~A[3], B[3]);  // AND_Gate
  xnor xnor_1 (xnor_1_out, A[3], B[3]);
  and and_2 (and_2_out, ~A[2], B[2]);  // AND_Gate
  xnor xnor_2 (xnor_2_out, A[2], B[2]);
  and and_3 (and_3_out, ~A[1], B[1]);  // AND_Gate
  xnor xnor_3 (xnor_3_out, A[1], B[1]);
  and and_4 (and_4_out, ~A[0], B[0]);  // AND_Gate
  and and_5 (and_5_out, xnor_1_out, Eq, and_2_out);
  and and_6 (and_6_out, Eq, xnor_1_out, xnor_2_out, and_3_out);
  and and_7 (and_7_out, xnor_1_out, xnor_2_out, Eq, xnor_3_out, and_4_out);
  or or_1 (S, and_1_out, and_5_out, and_6_out, and_7_out);
endmodule
